# Fritzing sketch Circuit-Diagram (saved by Fritzing 0.9.3b)
breadboards: 1

parts:
  LED1 = LED - 5mm [color="Red (633nm)" package="5 mm [THT]"]
  LED2 = LED - 5mm [color="Green (555nm)" package="5 mm [THT]"]
  S1 = Pushbutton [package="[THT]"]
  R1 = Resistor [tolerance=±5% resistance=220 package=THT]
  R2 = Resistor [tolerance=±5% resistance=220 package=THT]
  Raspberry_Pi_1 = Raspberry Pi 3 [part_number=RPI-3-V1.2]

nets:
  N1: LED1.cathode, R1.Pin_0
  N2: LED1.anode, Raspberry_Pi_1.GPIO17
  N3: LED2.cathode, R2.Pin_0
  N4: LED2.anode, Raspberry_Pi_1.GPIO27
  N5: S1.Pin_1, S1.Pin_2, R1.Pin_1, R2.Pin_1, Raspberry_Pi_1.GND
  N6: S1.Pin_3, S1.Pin_4, Raspberry_Pi_1.GPIO22
